# Fritzing sketch schematic (saved by Fritzing 1.0.0rc)
breadboards: 1

parts:
  Mod1 = Amica NodeMCU DEVKIT 1.0
  Grove1 = Grove OLED 128x96
  M1 = fc-51 [package=THT]  # not connected

nets:
  N1: Mod1.pin5, Mod1.pin_12, Mod1.pin_28
  N2: Mod1.pin8, Grove1.VCC
  N3: Mod1.pin_16, Mod1.pin_21, Mod1.pin_25, Mod1.pin_29
